// Logisim project ALU.circ as structural Verilog: 8 circuits, main circuit ALU32
module LeftShift32 (
  input  [31:0] B,
  input  C_in,
  input  [4:0] Sa,
  output [31:0] C
);

  wire [31:0] eight_bit_shifter_1_shifted, four_bit_shifter_1_shifted, multiplexer_1_out, multiplexer_2_out,
       multiplexer_3_out, multiplexer_4_out, one_bit_shifter_1_shifted, sixteen_bit_shifter_1_shifted,
       two_bit_shifter_1_shifted;

  one_bit_shifter one_bit_shifter_1 (.C_in(C_in), .B(B), .shifted(one_bit_shifter_1_shifted));
  Multiplexer #(.width(32), .enable("false")) multiplexer_1 (
    .in0(B), .in1(one_bit_shifter_1_shifted), .out(multiplexer_1_out), .sel(Sa[0]));
  Multiplexer #(.width(32), .enable("false")) multiplexer_2 (
    .in0(multiplexer_1_out), .in1(two_bit_shifter_1_shifted), .out(multiplexer_2_out), .sel(Sa[1]));
  two_bit_shifter two_bit_shifter_1 (.C_in(C_in), .B(multiplexer_1_out), .shifted(two_bit_shifter_1_shifted));
  Multiplexer #(.width(32), .enable("false")) multiplexer_3 (
    .in0(multiplexer_2_out), .in1(four_bit_shifter_1_shifted), .out(multiplexer_3_out), .sel(Sa[2]));
  four_bit_shifter four_bit_shifter_1 (.C_in(C_in), .B(multiplexer_2_out), .shifted(four_bit_shifter_1_shifted));
  eight_bit_shifter eight_bit_shifter_1 (.C_in(C_in), .B(multiplexer_3_out), .shifted(eight_bit_shifter_1_shifted));
  Multiplexer #(.width(32), .enable("false")) multiplexer_4 (
    .in0(multiplexer_3_out), .in1(eight_bit_shifter_1_shifted), .out(multiplexer_4_out), .sel(Sa[3]));
  sixteen_bit_shifter sixteen_bit_shifter_1 (
    .C_in(C_in), .B(multiplexer_4_out), .Shifted(sixteen_bit_shifter_1_shifted));
  Multiplexer #(.width(32), .enable("false")) multiplexer_5 (
    .in0(multiplexer_4_out), .in1(sixteen_bit_shifter_1_shifted), .out(C), .sel(Sa[4]));
endmodule

module Add32 (
  input  [31:0] A,
  input  [31:0] B,
  input  Cin,
  output [31:0] C,
  output V
);


  // Notes on the sheet:
  //   Do not delete or rename any of the input or output pins, and do not add any other pins.
  //   (It's fine to move the pins around, though)
endmodule

module ALU32 (
  input  [31:0] A,
  input  [31:0] B,
  input  [3:0] Op,
  input  [4:0] Sa,
  output [31:0] C,
  output V
);


  // Notes on the sheet:
  //   Do not delete or rename any of the input or output pins, and do not add any other pins.
  //   (It's fine to move the pins around, though)
endmodule

module one_bit_shifter (
  input  C_in,
  input  [31:0] B,
  output [31:0] shifted
);


  assign shifted = {B[30:0], C_in};
endmodule

module two_bit_shifter (
  input  C_in,
  input  [31:0] B,
  output [31:0] shifted
);

  wire [31:0] one_bit_shifter_1_shifted;

  one_bit_shifter one_bit_shifter_1 (.C_in(C_in), .B(B), .shifted(one_bit_shifter_1_shifted));
  one_bit_shifter one_bit_shifter_2 (.C_in(C_in), .B(one_bit_shifter_1_shifted), .shifted(shifted));
endmodule

module four_bit_shifter (
  input  C_in,
  input  [31:0] B,
  output [31:0] shifted
);

  wire [31:0] two_bit_shifter_1_shifted;

  two_bit_shifter two_bit_shifter_1 (.C_in(C_in), .B(B), .shifted(two_bit_shifter_1_shifted));
  two_bit_shifter two_bit_shifter_2 (.C_in(C_in), .B(two_bit_shifter_1_shifted), .shifted(shifted));
endmodule

module eight_bit_shifter (
  input  C_in,
  input  [31:0] B,
  output [31:0] shifted
);

  wire [31:0] four_bit_shifter_1_shifted;

  four_bit_shifter four_bit_shifter_1 (.C_in(C_in), .B(B), .shifted(four_bit_shifter_1_shifted));
  four_bit_shifter four_bit_shifter_2 (.C_in(C_in), .B(four_bit_shifter_1_shifted), .shifted(shifted));
endmodule

module sixteen_bit_shifter (
  input  C_in,
  input  [31:0] B,
  output [31:0] Shifted
);

  wire [31:0] eight_bit_shifter_1_shifted;

  eight_bit_shifter eight_bit_shifter_1 (.C_in(C_in), .B(B), .shifted(eight_bit_shifter_1_shifted));
  eight_bit_shifter eight_bit_shifter_2 (.C_in(C_in), .B(eight_bit_shifter_1_shifted), .shifted(Shifted));
endmodule
